# Fritzing sketch schematic (saved by Fritzing 0.9.2b)
breadboards: 1

parts:
  Part1 = Arduino Ethernet Shield (Rev3)
  RHT2 = Humidity and Temperature Sensor RHT03
  R1 = Photocell (LDR) [package=THT]
  LED1 = smd LED [color="Red (633nm)" package="0603 [SMD]"]
  R2 = Resistor [tolerance=±5% resistance=10k package="2010 [SMD]"]
  R3 = Resistor [tolerance=±5% resistance=330 package=THT]

nets:
  N1: Part1.A0, R1.pin_1, R2.Pin_0
  N2: Part1.PWM_D5, RHT2.Data-signal
  N3: Part1.PWM_D6, R3.Pin_0
  5V: Part1.5V, RHT2.Vcc, R1.pin_0
  N4: Part1.GND, RHT2.GND_1, LED1.anode, R2.Pin_1
  N5: LED1.cathode, R3.Pin_1
